# Fritzing sketch Ir_sniffer_circuit (saved by Fritzing 0.9.3b)
breadboards: 1

parts:
  Composant1 = Arduino Uno (Rev3)
  Tsop_31238 = TSOP312.., 314.. [package=THT]
  R2 = Resistor [tolerance=±5% resistance=100 package=THT]
  C1 = Ceramic Capacitor [capacitance=4.7µF package="100 mil [THT, multilayer]"]
  Composant2 = Lilypad Power Supply

nets:
  GND: Composant1.GND, Tsop_31238.GND, C1.0, Composant2.GND
  N1: Composant1.D6_PWM, Tsop_31238.Data
  N2: Composant1.VIN, R2.Pin_1, Composant2.+
  N3: Tsop_31238.Vs, R2.Pin_0, C1.1

notes:
  Tsop31238
  100Ω  Resistor
  4.7 uf capacitor
  5v power supply
  Arduino Uno
